# Fritzing sketch esquema sigue lineas (saved by Fritzing 0.9.3b)
breadboards: 1

parts:
  Componente1 = iceZUM Alhambra
  Componente2 = Motor Driver 1A Dual TB6612FNG
  M1 = DC Motor
  M2 = DC Motor
  U1 = Ambient Light Sensor [package=temt6000-sen]
  U2 = Ambient Light Sensor [package=temt6000-sen]
  U3 = Ambient Light Sensor [package=temt6000-sen]
  U4 = Ambient Light Sensor [package=temt6000-sen]

nets:
  N1: Componente1.D0, Componente1.V0, Componente2.BIN2, U2.C1, U2.E1
  N2: Componente1.D1, Componente1.V1, Componente2.BIN1, U1.C1, U1.E1
  N3: Componente1.D2, Componente1.V2, Componente2.AIN2, U3.C1, U3.E1
  N4: Componente1.D3, Componente1.V3, Componente2.AIN1, U4.C1, U4.E1
  N5: Componente1.5VP, Componente2.VCC
  N6: Componente2.B01, M2.pin_2
  N7: Componente2.B02, M2.pin_1
  N8: Componente2.A02, M1.pin_1
  N9: Componente2.A01, M1.pin_2

custom parts:
  iceZUM Alhambra: Arduino/zum compatible Open FPGA electronic board. Synthesize hardware easily, using only open source tools
