# Fritzing sketch ESQUEMA10 (saved by Fritzing 0.9.3b)
breadboards: 1

parts:
  Componente1 = Motor Driver 1A Dual TB6612FNG
  IC1 = Hex Inverter Schmitt Trigger SN74HC14 [package="DIP (Dual Inline)"]
  Componente3 = iceZUM Alhambra
  M1 = DC Motor
  Q1 = PHOTOTRANSISTOR REFLECTIVE OBJECT SENSOR [package=qrb1114-side]
  Q2 = PHOTOTRANSISTOR REFLECTIVE OBJECT SENSOR [package=qrb1114-side]
  Q3 = PHOTOTRANSISTOR REFLECTIVE OBJECT SENSOR [package=qrb1114-side]
  Q4 = PHOTOTRANSISTOR REFLECTIVE OBJECT SENSOR [package=qrb1114-side]
  M2 = DC Motor
  VCC1 = Battery block 9V
  Power_plug1 = Power plug
  D1 = Rectifier Diode [package="Melf DO-213 AA [SMD]"]
  D2 = Rectifier Diode [package="Melf DO-213 AA [SMD]"]
  R1 = Resistor [tolerance=±5% resistance=220 package="2010 [SMD]"]  # not connected
  R2 = Resistor [tolerance=±5% resistance=220 package="2010 [SMD]"]  # not connected
  R3 = Resistor [tolerance=±5% resistance=220 package="2010 [SMD]"]  # not connected
  R4 = Resistor [tolerance=±5% resistance=220 package="2010 [SMD]"]  # not connected

nets:
  GND: Componente1.GND, IC1.GND, Componente3.GND, Q1.K, Q2.K, Q3.K, Q4.K, VCC1.-, Power_plug1.GND
  N1: Componente1.B01, M2.pin_2
  N2: Componente1.B02, M2.pin_1
  N3: Componente1.A02, M1.pin_2
  N4: Componente1.A01, M1.pin_1
  VCC: Componente1.VCC, Componente1.STBY, Componente3.5V
  N5: Componente1.VM, D2.cathode
  N6: Componente1.PWMA, Componente3.D8, Componente3.V8
  N7: Componente1.AIN2, Componente3.D5, Componente3.V5
  N8: Componente1.AIN1, Componente3.D4, Componente3.V4
  N9: Componente1.BIN1, Componente3.D6, Componente3.V6
  N10: Componente1.BIN2, Componente3.D7, Componente3.V7
  N11: Componente1.PWMB, Componente3.D9
  N12: IC1.1Y, Componente3.D0, Componente3.V0
  N13: IC1.2Y, Componente3.D1, Componente3.V1
  N14: IC1.3Y, Componente3.D2, Componente3.V2
  N15: IC1.4Y, Componente3.D3, Componente3.V3
  VCC_2: IC1.VCC, Q1.A, Q2.A, Q3.A, Q4.A, VCC1.+, Power_plug1.VCC, D1.anode
  N16: Q1.C, Q2.C, Q3.C, Q4.C

custom parts:
  iceZUM Alhambra: Arduino/zum compatible Open FPGA electronic board. Synthesize hardware easily, using only open source tools
